// Logisim project 17-ControlUpgraded.circ as structural Verilog: 1 circuit, main circuit main
// twosComplement
module main (
  input  RST,
  input  [3:0] DATA,
  input  EN,
  input  RST_2,
  input  EN_2,
  input  [3:0] DATA_2,
  input  RST_3,
  input  [3:0] DATA_3,
  input  EN_3,
  input  RST_4,
  input  EN_4,
  input  [3:0] DATA_4,
  output out_13,
  output out_14,
  output out_15,
  output out_16
);

  wire A_2_qn, A_3_qn, A_4_q, A_4_qn, A_qn, ADD, ADD2, adder_1_cout, adder_2_cout, and_1_out, and_2_out,
       and_3_out, and_4_out, and_5_out, and_6_out, B_2_qn, B_3_q, B_3_qn, B_4_q, B_4_qn, B_qn, CAP, CAP2,
       clock_1_out, clock_2_out, clock_3_out, clock_4_out, CLR, CLR2, LDA, LDA2, LDB, LDB2, LDC, LDC2, LDRA,
       LDRA2, LDRB, LDRB2, multiplexer_1_out, multiplexer_2_out, multiplexer_3_out, multiplexer_4_out,
       not_1_out, not_2_out, or_1_out, or_2_out, or_3_out, or_4_out, or_5_out, xor_1_out, xor_2_out;
  wire [1:0] A_2_q;
  wire [1:1] B_q;
  wire [3:0] adder_1_out, adder_2_out, controlled_buffer_1_out, controlled_buffer_2_out,
       controlled_buffer_3_out, controlled_buffer_4_out, controlled_buffer_5_out, controlled_buffer_6_out,
       RA_2_q, RA_q, RB_2_q, RB_q, register_1_q, register_2_q, register_3_q, register_4_q;

  Clock clock_1 (.out(clock_1_out));
  Clock clock_2 (.out(clock_2_out));
  Clock clock_3 (.out(clock_3_out));
  Clock clock_4 (.out(clock_4_out));
  and and_1 (and_1_out, ADD, B_3_qn);
  or or_1 (or_1_out, ADD, B_3_qn);
  or or_2 (or_2_out, A_4_qn, B_4_qn);
  and and_2 (and_2_out, B_4_q, out_14);
  or or_3 (or_3_out, and_2_out, A_4_q);
  D_Flip_Flop A (
    .clk(clock_3_out), .D(multiplexer_2_out), .Q(ADD2), .Qn(A_qn), .en(EN_3), .reset(RST_3));  // open: preset
  D_Flip_Flop B (
    .clk(clock_3_out), .D(multiplexer_1_out), .Q(B_q[1]), .Qn(B_qn), .en(EN_3), .reset(RST_3));  // open: preset
  Multiplexer #(.select(2)) multiplexer_1 (
    .in0(1'b0), .in1(1'b1), .in2(1'b0), .in3(1'b0), .out(multiplexer_1_out), .sel({B_q[1], ADD2}), .en(EN_3));
  Multiplexer #(.select(2)) multiplexer_2 (
    .in0(1'b1), .in1(1'b1), .in2(1'b0), .in3(1'b1), .out(multiplexer_2_out), .sel({B_q[1], ADD2}), .en(EN_3));
  D_Flip_Flop A_2 (
    .clk(clock_4_out), .D(multiplexer_3_out), .Q(A_2_q[0]), .Qn(A_2_qn), .en(EN_4), .reset(RST_4));  // open: preset
  D_Flip_Flop B_2 (
    .clk(clock_4_out), .D(multiplexer_4_out), .Q(A_2_q[1]), .Qn(B_2_qn), .en(EN_4), .reset(RST_4));  // open: preset
  Multiplexer #(.select(2)) multiplexer_3 (
    .in0(1'b1), .in1(1'b1), .in2(1'b1), .in3(1'b0), .out(multiplexer_3_out), .sel(A_2_q), .en(EN_4));
  Multiplexer #(.select(2)) multiplexer_4 (
    .in0(1'b0), .in1(1'b1), .in2(out_16), .in3(1'b1), .out(multiplexer_4_out), .sel(A_2_q), .en(EN_4));
  D_Flip_Flop A_3 (.clk(clock_1_out), .D(or_1_out), .Q(ADD), .Qn(A_3_qn), .en(EN), .reset(RST));  // open: preset
  D_Flip_Flop B_3 (.clk(clock_1_out), .D(and_1_out), .Q(B_3_q), .Qn(B_3_qn), .en(EN), .reset(RST));  // open: preset
  D_Flip_Flop A_4 (.clk(clock_2_out), .D(or_2_out), .Q(A_4_q), .Qn(A_4_qn), .en(EN_2), .reset(RST_2));  // open: preset
  D_Flip_Flop B_4 (.clk(clock_2_out), .D(or_3_out), .Q(B_4_q), .Qn(B_4_qn), .en(EN_2), .reset(RST_2));  // open: preset
  not not_1 (not_1_out, clock_1_out);
  not not_2 (not_2_out, clock_3_out);
  and and_3 (and_3_out, B_qn, A_qn);
  and and_4 (and_4_out, ADD2, B_q[1]);
  and and_5 (and_5_out, B_3_qn, A_3_qn);
  buf or_4 (or_4_out, and_6_out);  // OR_Gate
  and and_6 (and_6_out, ADD, B_3_q);
  xor xor_1 (xor_1_out, ADD, B_3_q);
  and and_7 (CAP, B_4_q, A_4_qn);
  and and_8 (LDRA, B_4_qn, A_4_q);
  xnor xnor_1 (LDRB, A_4_q, B_4_q);
  buf or_5 (or_5_out, and_4_out);  // OR_Gate
  xor xor_2 (xor_2_out, ADD2, B_q[1]);
  and and_9 (CAP2, A_2_q[1], A_2_qn);
  and and_10 (LDRA2, B_2_qn, A_2_q[0]);
  xnor xnor_2 (LDRB2, A_2_q[0], A_2_q[1]);
  // XOR_Gate xor_3 is placed but not wired
  // AND_Gate and_11 is placed but not wired
  and u_LDA (LDA, or_4_out, not_1_out);
  and u_LDB (LDB, xor_1_out, not_1_out);
  and u_LDC (LDC, B_3_q, A_3_qn, not_1_out);
  and u_CLR (CLR, B_3_qn, A_3_qn);
  // XOR_Gate xor_4 is placed but not wired
  // AND_Gate and_12 is placed but not wired
  and LDA_2 (LDA2, or_5_out, not_2_out);
  and LDB_2 (LDB2, xor_2_out, not_2_out);
  and LDC_2 (LDC2, B_q[1], A_qn, not_2_out);
  and CLR_2 (CLR2, B_qn, A_qn);
  // OR_Gate or_6 is placed but not wired
  // OR_Gate or_7 is placed but not wired
  Register #(.width(4)) register_1 (.D(DATA), .en(EN), .Q(register_1_q), .clk(LDA), .clr(RST));
  Register #(.width(4)) register_2 (.D(adder_1_out), .en(EN), .Q(register_2_q), .clk(LDB), .clr(RST));
  Register #(.width(4)) RA (.D(RB_q), .Q(RA_q), .clk(LDRA), .clr(RST_2));  // open: en
  Register #(.width(4)) RB (.D(DATA_2), .Q(RB_q), .clk(LDRB), .clr(RST_2));  // open: en
  Register #(.width(4)) register_3 (.D(DATA_3), .en(EN_3), .Q(register_3_q), .clk(LDA2), .clr(RST_3));
  Register #(.width(4)) register_4 (.D(adder_2_out), .en(EN_3), .Q(register_4_q), .clk(LDB2), .clr(RST_3));
  Register #(.width(4)) RA_2 (.D(RB_2_q), .Q(RA_2_q), .clk(LDRA2), .clr(RST_4));  // open: en
  Register #(.width(4)) RB_2 (.D(DATA_4), .Q(RB_2_q), .clk(LDRB2), .clr(RST_4));  // open: en
  assign controlled_buffer_1_out = ADD ? register_2_q : 4'bz;  // Controlled_Buffer controlled_buffer_1
  assign controlled_buffer_2_out = CAP ? RA_q : 4'bz;  // Controlled_Buffer controlled_buffer_2
  assign controlled_buffer_3_out = CAP ? RB_q : 4'bz;  // Controlled_Buffer controlled_buffer_3
  assign controlled_buffer_4_out = ADD2 ? register_4_q : 4'bz;  // Controlled_Buffer controlled_buffer_4
  assign controlled_buffer_5_out = CAP2 ? RA_2_q : 4'bz;  // Controlled_Buffer controlled_buffer_5
  assign controlled_buffer_6_out = CAP2 ? RB_2_q : 4'bz;  // Controlled_Buffer controlled_buffer_6
  Adder #(.width(4)) adder_1 (
    .a(register_1_q), .b(controlled_buffer_1_out), .out(adder_1_out), .cout(adder_1_cout));  // open: cin
  Comparator #(.width(4)) comparator_1 (
    .a(controlled_buffer_2_out), .b(controlled_buffer_3_out), .gt(out_14));  // open: eq, lt
  Adder #(.width(4)) adder_2 (
    .a(register_3_q), .b(controlled_buffer_4_out), .out(adder_2_out), .cout(adder_2_cout));  // open: cin
  Comparator #(.width(4)) comparator_2 (
    .a(controlled_buffer_5_out), .b(controlled_buffer_6_out), .gt(out_16));  // open: eq, lt
  Register #(.width(1)) register_5 (.D(adder_1_cout), .en(EN), .Q(out_13), .clk(LDC), .clr(CLR));
  Register #(.width(1)) register_6 (.D(adder_2_cout), .en(EN_3), .Q(out_15), .clk(LDC2), .clr(CLR2));

  // Other names for the same wires on the sheet: EN2 = EN_3; Z = out_14; Z2 = out_16

  // Notes on the sheet:
  //   加法控制器（计数器型）
  //   比较控制器（计数器型）
  //   加法控制器（选择器型）
  //   比较控制器（选择器型）
  //   MUXA
  //   MUXB
endmodule
